// Logisim project s-mips.circ as structural Verilog: 24 circuits, main circuit S-MIPS Board
module S_MIPS_Board (
  input  DESHABILITAR_DISPATCHER,
  output halt
);

  wire button_1_out, CLK, CS, d_ff_1_q, LCLR, LoadRAM, LoadRAMOn, LW, R_R_W, R_W, ram_dispatcher_1_finished,
       RCS, Reset_out, RST, TTY_EN;
  wire [2:0] KDB;
  wire [3:0] LMask, Mask, ram_1_read_time, ram_1_write_time, RMask;
  wire [6:0] KDB_DATA, TTY_DATA;
  wire [15:0] Addr, LAddr, RAddr;
  wire [31:0] I0, I1, I2, I3, LData, ram_1_data_out_0, ram_1_data_out_1, ram_1_data_out_2, ram_1_data_out_3,
       RI0, RI1, RI2, RI3;

  TTY #(.rows(25), .cols(80)) tty_1 (.data(TTY_DATA), .clk(CLK), .we(TTY_EN), .clr(RST));
  not not_1 (LoadRAMOn, ram_dispatcher_1_finished);
  RAM_Dispatcher ram_dispatcher_1 (
    .WriteTime(ram_1_write_time), .Clock(CLK), .Data(LData), .Address(LAddr), .Mask(LMask),
    .Finished(ram_dispatcher_1_finished), .Write(LW), .CLR(LCLR));
  Keyboard #(.buflen(64)) keyboard_1 (.clk(CLK), .re(KDB[0]), .avail(KDB[2]), .data(KDB_DATA));  // open: clr
  RAM ram_1 (
    .Address(RAddr), .Data_Out_0(ram_1_data_out_0), .Data_Out_1(ram_1_data_out_1),
    .Data_Out_2(ram_1_data_out_2), .Data_Out_3(ram_1_data_out_3), .Data_In_0(RI0), .Data_In_1(RI1),
    .Data_In_2(RI2), .Data_In_3(RI3), .Mask(RMask), .nRead_Write(R_R_W), .Chip_Select(RCS),
    .Read_Time(ram_1_read_time), .Reset(button_1_out), .Write_Time(ram_1_write_time));
  Button button_1 (.out(button_1_out));
  D_Flip_Flop d_ff_1 (.clk(CLK), .D(1'b1), .Q(d_ff_1_q), .reset(Reset_out));  // open: Qn, preset, en
  Button Reset (.out(Reset_out));
  S_MIPS s_mips_1 (
    .Kbd_Enable(KDB[0]), .Address(Addr), .Kbd_Clear(KDB[1]), .Kbd_Available(KDB[2]), .RAM_In_0(I0),
    .Kbd_ASCII_Data(KDB_DATA), .RAM_In_1(I1), .TTY_Enable(TTY_EN), .RAM_In_2(I2), .RAM_In_3(I3),
    .TTY_ASCII_Data(TTY_DATA), .Reset(RST), .RAM_Out_0(ram_1_data_out_0), .Clock(CLK),
    .RAM_Out_1(ram_1_data_out_1), .Stop(halt), .RAM_Out_2(ram_1_data_out_2), .RAM_Out_3(ram_1_data_out_3),
    .Mask(Mask), .Read_Time(ram_1_read_time), .Write_Time(ram_1_write_time), .nRead_Write(R_W),
    .Chip_Select(CS));
  D_Flip_Flop d_ff_2 (.clk(CLK), .D(d_ff_1_q), .Qn(LCLR), .reset(Reset_out));  // open: Q, preset, en
  or or_1 (RST, LCLR, LoadRAM);
  Clock clock_1 (.out(CLK));
  // Probe on TTY_DATA
  Multiplexer #(.width(32), .enable("false")) multiplexer_1 (.in0(I0), .in1(LData), .out(RI0), .sel(LoadRAM));
  Multiplexer #(.width(32), .enable("false")) multiplexer_2 (.in0(I1), .in1(LData), .out(RI1), .sel(LoadRAM));
  Multiplexer #(.width(32), .enable("false")) multiplexer_3 (.in0(I2), .in1(LData), .out(RI2), .sel(LoadRAM));
  Multiplexer #(.width(32), .enable("false")) multiplexer_4 (.in0(I3), .in1(LData), .out(RI3), .sel(LoadRAM));
  and and_1 (LoadRAM, ~DESHABILITAR_DISPATCHER, LoadRAMOn);  // AND_Gate
  Multiplexer #(.width(16), .enable("false")) multiplexer_5 (.in0(Addr), .in1(LAddr), .out(RAddr), .sel(LoadRAM));
  Multiplexer #(.width(4), .enable("false")) multiplexer_6 (.in0(Mask), .in1(LMask), .out(RMask), .sel(LoadRAM));
  Multiplexer #(.enable("false")) multiplexer_7 (.in0(CS), .in1(LW), .out(RCS), .sel(LoadRAM));
  Multiplexer #(.enable("false")) multiplexer_8 (.in0(R_W), .in1(LW), .out(R_R_W), .sel(LoadRAM));

  // Notes on the sheet:
  //   NO MODIFICAR
  //   Keyboard
endmodule

module RAM (
  input  [15:0] Address,
  input  [31:0] Data_In_0,
  input  [31:0] Data_In_1,
  input  [31:0] Data_In_2,
  input  [31:0] Data_In_3,
  input  [3:0] Mask,
  input  nRead_Write,
  input  Chip_Select,
  input  Reset,
  output [31:0] Data_Out_0,
  output [31:0] Data_Out_1,
  output [31:0] Data_Out_2,
  output [31:0] Data_Out_3,
  output [3:0] Read_Time,
  output [3:0] Write_Time
);

  wire and_2_out, and_3_out, and_4_out, and_5_out, and_6_out, and_7_out, and_8_out, and_9_out, Changed, CLK,
       comparator_2_eq, comparator_3_eq, comparator_4_eq, comparator_5_eq, comparator_6_eq, Count,
       demultiplexer_3_out0, Idle, Idle_q, Load, Load0, Load1, nand_1_out, or_1_out, or_2_out, or_3_out,
       or_4_out, or_5_out, or_6_out, or_7_out, or_8_out, or_9_out, or_10_out, Proc_q, Update_Mem, Zero_Time;
  wire [3:0] counter_1_q, multiplexer_1_out, subtractor_1_out;
  wire [31:0] register_1_q, register_2_q, register_3_q, register_4_q, register_5_q;

  // Probe on 4'b0011
  // Probe on 4'b0010
  Multiplexer #(.width(4), .enable("false")) multiplexer_1 (
    .in0(4'b0011), .in1(4'b0010), .out(multiplexer_1_out), .sel(nRead_Write));
  or or_1 (or_1_out, Idle, Update_Mem);
  or or_2 (or_2_out, ~Chip_Select, Reset);  // OR_Gate
  Subtractor #(.width(4)) subtractor_1 (.a(multiplexer_1_out), .b(4'b0010), .out(subtractor_1_out));  // open: bin, bout
  Demultiplexer #(.enable("false")) demultiplexer_1 (.out0(Idle), .out1(Load0), .in(Idle_q), .sel(Changed));
  D_Flip_Flop u_Idle (.clk(CLK), .D(or_1_out), .Q(Idle_q), .preset(or_2_out));  // open: Qn, en, reset
  // Probe on counter_1_q
  Counter #(.width(4), .max('hf)) counter_1 (
    .load(Load), .D(subtractor_1_out), .count(Count), .Q(counter_1_q), .clk(CLK), .clr(or_3_out));  // open: carry
  or or_3 (or_3_out, ~Chip_Select, Reset);  // OR_Gate
  Comparator #(.width(4), .mode("unsigned")) comparator_1 (
    .a(4'b0000), .b(counter_1_q), .eq(Zero_Time));  // open: gt, lt
  or or_4 (or_4_out, Count, Load0, Load1);
  Register #(.width(32)) register_1 (.D(Data_In_0), .en(Chip_Select), .Q(register_1_q), .clk(CLK), .clr(or_5_out));
  or or_5 (or_5_out, ~Chip_Select, Reset);  // OR_Gate
  Register #(.width(32)) register_2 (.D(Data_In_1), .en(Chip_Select), .Q(register_2_q), .clk(CLK), .clr(or_6_out));
  or or_6 (or_6_out, ~Chip_Select, Reset);  // OR_Gate
  Register #(.width(32)) register_3 (.D(Data_In_2), .en(Chip_Select), .Q(register_3_q), .clk(CLK), .clr(or_7_out));
  or or_7 (or_7_out, ~Chip_Select, Reset);  // OR_Gate
  Register #(.width(32)) register_4 (.D(Data_In_3), .en(Chip_Select), .Q(register_4_q), .clk(CLK), .clr(or_8_out));
  or or_8 (or_8_out, ~Chip_Select, Reset);  // OR_Gate
  Register #(.width(32)) register_5 (
    .D({{11{1'b1}}, nRead_Write, Mask, Address}), .en(Chip_Select), .Q(register_5_q), .clk(CLK),
    .clr(or_9_out));
  or or_9 (or_9_out, ~Chip_Select, Reset);  // OR_Gate
  D_Flip_Flop Proc (.clk(CLK), .D(or_4_out), .Q(Proc_q), .reset(or_10_out));  // open: Qn, preset, en
  or or_10 (or_10_out, ~Chip_Select, Reset);  // OR_Gate
  Demultiplexer #(.enable("false")) demultiplexer_2 (
    .out0(Count), .out1(Update_Mem), .in(demultiplexer_3_out0), .sel(Zero_Time));
  Demultiplexer #(.enable("false")) demultiplexer_3 (
    .out0(demultiplexer_3_out0), .out1(Load1), .in(Proc_q), .sel(Changed));
  Clock clock_1 (.out(CLK));
  Comparator #(.width(32)) comparator_2 (.a(register_1_q), .b(Data_In_0), .eq(comparator_2_eq));  // open: gt, lt
  Comparator #(.width(32)) comparator_3 (.a(register_2_q), .b(Data_In_1), .eq(comparator_3_eq));  // open: gt, lt
  Comparator #(.width(32)) comparator_4 (.a(register_3_q), .b(Data_In_2), .eq(comparator_4_eq));  // open: gt, lt
  Comparator #(.width(32)) comparator_5 (.a(register_4_q), .b(Data_In_3), .eq(comparator_5_eq));  // open: gt, lt
  Comparator #(.width(32)) comparator_6 (
    .a(register_5_q), .b({{11{1'b1}}, nRead_Write, Mask, Address}), .eq(comparator_6_eq));  // open: gt, lt
  nand nand_1 (nand_1_out, comparator_6_eq, comparator_2_eq, comparator_3_eq, comparator_4_eq, comparator_5_eq);
  and and_1 (Changed, nand_1_out, Chip_Select);
  or or_11 (Load, Count, Load1, Load0);
  and and_2 (and_2_out, Mask[0], Update_Mem, nRead_Write);
  and and_3 (and_3_out, Mask[1], Update_Mem, nRead_Write);
  and and_4 (and_4_out, Mask[2], Update_Mem, nRead_Write);
  and and_5 (and_5_out, Mask[3], Update_Mem, nRead_Write);
  RAM_part #(.addrWidth(16), .dataWidth(32), .bus("separate")) ram_1 (
    .addr(Address), .din(Data_In_0), .data(Data_Out_0), .str(and_2_out), .sel(Chip_Select), .clk(CLK),
    .ld(and_6_out), .clr(Reset));
  and and_6 (and_6_out, ~nRead_Write, Idle);  // AND_Gate
  RAM_part #(.addrWidth(16), .dataWidth(32), .bus("separate")) ram_2 (
    .addr(Address), .din(Data_In_1), .data(Data_Out_1), .str(and_3_out), .sel(Chip_Select), .clk(CLK),
    .ld(and_7_out), .clr(Reset));
  and and_7 (and_7_out, ~nRead_Write, Idle);  // AND_Gate
  RAM_part #(.addrWidth(16), .dataWidth(32), .bus("separate")) ram_3 (
    .addr(Address), .din(Data_In_2), .data(Data_Out_2), .str(and_4_out), .sel(Chip_Select), .clk(CLK),
    .ld(and_8_out), .clr(Reset));
  and and_8 (and_8_out, ~nRead_Write, Idle);  // AND_Gate
  RAM_part #(.addrWidth(16), .dataWidth(32), .bus("separate")) ram_4 (
    .addr(Address), .din(Data_In_3), .data(Data_Out_3), .str(and_5_out), .sel(Chip_Select), .clk(CLK),
    .ld(and_9_out), .clr(Reset));
  and and_9 (and_9_out, ~nRead_Write, Idle);  // AND_Gate

  assign Read_Time = 4'b0011;
  assign Write_Time = 4'b0010;

  // Other names for the same wires on the sheet: M0 = Mask[0]; M1 = Mask[1]; M2 = Mask[2]; M3 = Mask[3];
  //   RW = nRead_Write; CLR = Reset; CS = Chip_Select; Load2 = Count

  // Notes on the sheet:
  //   NO MODIFICAR
  //   excepto quizás los valores RT y WT
  //   BANK0
  //   BANK1
  //   BANK2
  //   BANK3
endmodule

module S_MIPS (
  input  Kbd_Available,
  input  [6:0] Kbd_ASCII_Data,
  input  [31:0] RAM_Out_0,
  input  [31:0] RAM_Out_1,
  input  Reset,
  input  [31:0] RAM_Out_2,
  input  Clock,
  input  [31:0] RAM_Out_3,
  input  [3:0] Read_Time,
  input  [3:0] Write_Time,
  output Kbd_Enable,
  output [15:0] Address,
  output Kbd_Clear,
  output TTY_Enable,
  output [6:0] TTY_ASCII_Data,
  output Stop,
  output [31:0] RAM_In_0,
  output [31:0] RAM_In_1,
  output [31:0] RAM_In_2,
  output [31:0] RAM_In_3,
  output [3:0] Mask,
  output nRead_Write,
  output Chip_Select
);

  wire ALU_inst, d_ff_2_q, EGI, jmp_inst, mem_inst, or_1_out, or_2_out, PC_Enable, R_inst, Read_Data,
       Read_Inst, ready_data, ready_inst, ready_write, RF_RW, stack_inst, start, tty, Write, write_inst;
  wire [31:0] instruction, MAddress, Memorie_ram_in_0, Memorie_ram_in_1, Memorie_ram_in_2, Memorie_ram_in_3,
       multiplexer_1_out, multiplexer_2_out, multiplexer_3_out, multiplexer_4_out;

  D_Flip_Flop #(.trigger("falling")) d_ff_1 (.clk(Clock), .D(Reset), .Q(start));  // open: Qn, preset, en, reset
  // Probe on TTY_ASCII_Data
  or or_1 (or_1_out, Read_Inst, ready_inst);
  D_Flip_Flop #(.trigger("falling")) d_ff_2 (
    .clk(Clock), .D(Read_Inst), .Q(d_ff_2_q), .en(or_1_out));  // open: Qn, preset, reset
  or or_2 (or_2_out, mem_inst, stack_inst);
  Multiplexer #(.width(32), .enable("false")) multiplexer_1 (
    .in0(RAM_Out_0), .in1(RAM_In_0), .out(multiplexer_1_out), .sel(Write));
  Multiplexer #(.width(32), .enable("false")) multiplexer_2 (
    .in0(RAM_Out_1), .in1(RAM_In_0), .out(multiplexer_2_out), .sel(Write));
  Multiplexer #(.width(32), .enable("false")) multiplexer_3 (
    .in0(RAM_Out_2), .in1(RAM_In_0), .out(multiplexer_3_out), .sel(Write));
  Multiplexer #(.width(32), .enable("false")) multiplexer_4 (
    .in0(RAM_Out_3), .in1(RAM_In_0), .out(multiplexer_4_out), .sel(Write));
  Control_Unit control_unit_1 (
    .in_1(Clock), .in_2(start), .in_3(Chip_Select), .in_4(ready_inst), .in_5(ready_write),
    .Read_Inst(Read_Inst), .Read_Data(Read_Data), .Write(Write), .Output(PC_Enable), .En_Get_Inst(EGI),
    .Instrucciones(ALU_inst), .in_8(R_inst), .in_13(Reset), .in_12(tty), .in_10(jmp_inst), .in_9(or_2_out),
    .in_11(write_inst), .in_6(ready_data), .Output_2(TTY_Enable), .Output_3(Kbd_Enable), .Output_4(Stop),
    .Output_5(RF_RW));
  Data_Path Data_Path (
    .in_1(instruction), .Reset(Clock), .Clock(Reset), .En_Get_Inst(EGI), .Is_PC(d_ff_2_q), .En_PC(PC_Enable),
    .Kbd_ASCII_Data(Kbd_ASCII_Data), .Output(MAddress),
    .R({RAM_In_0[7:0], RAM_In_0[15:8], RAM_In_0[23:16], RAM_In_0[31:24]}), .stop(Stop), .ALU_inst(ALU_inst),
    .R_instr(R_inst), .jmp(jmp_inst), .tty_en(tty), .Memorie_Inst(mem_inst), .Stack_inst(stack_inst),
    .Write_inst(write_inst), .Output_2(TTY_ASCII_Data), .in_8(RF_RW));
  Memorie Memorie (
    .RAM_In_0(Memorie_ram_in_0), .Address(MAddress), .RAM_In_1(Memorie_ram_in_1),
    .RAM_Out_0(multiplexer_1_out), .RAM_In_2(Memorie_ram_in_2), .RAM_Out_1(multiplexer_2_out),
    .RAM_In_3(Memorie_ram_in_3), .RAM_Out_2(multiplexer_3_out), .Output(Address),
    .RAM_Out_3(multiplexer_4_out), .Output_2(Mask), .Output_3(Chip_Select), .in_6(Read_Time),
    .Output_4(nRead_Write), .in_7(Write_Time), .Output_5(ready_inst), .Clock(Clock), .Output_6(ready_data),
    .Reset(Reset), .Output_7(ready_write), .Write(Write), .Obtain_Inst(Read_Inst), .Obtain_Data(Read_Data),
    .Is_Instruction(EGI), .Halt(Stop));
  // Probe on {RAM_In_0[7:0], RAM_In_0[15:8], RAM_In_0[23:16], RAM_In_0[31:24]}
  Multiplexer #(.select(2), .width(32), .enable("false")) multiplexer_5 (
    .in0(Memorie_ram_in_0), .in1(Memorie_ram_in_1), .in2(Memorie_ram_in_2), .in3(Memorie_ram_in_3),
    .out(instruction), .sel(MAddress[3:2]));
  // Probe on MAddress[3:2]
  // Probe on MAddress

  assign Kbd_Clear = Reset;
  assign RAM_In_1 = RAM_In_0;
  assign RAM_In_2 = RAM_In_0;
  assign RAM_In_3 = RAM_In_0;

  // Other names for the same wires on the sheet: CLK = Clock; CLR = Reset; CS = Chip_Select;
  //   KBD_AVAIL = Kbd_Available; KBD_DATA[6:0] = Kbd_ASCII_Data; R[31:0] = RAM_In_0; RAM_A[15:0] = Address;
  //   RAM_MASK[3:0] = Mask; RAM_OUTPUT_0[31:0] = RAM_Out_0; RAM_OUTPUT_1[31:0] = RAM_Out_1;
  //   RAM_OUTPUT_2[31:0] = RAM_Out_2; RAM_OUTPUT_3[31:0] = RAM_Out_3; RW = nRead_Write;
  //   TTY_DATA[6:0] = TTY_ASCII_Data

  // Notes on the sheet:
  //   RAM ADDRESS
  //   DATA FROM RAM
  //   DATA TO RAM
  //   DATA WRITE MASK
  //   RAM TIMING
  //   RAM CONTROL
  //   KEYBOARD
  //   TTY
  //   SEQUENCING
endmodule

module RAM_Dispatcher (
  input  [3:0] WriteTime,
  input  Clock,
  input  CLR,
  output [31:0] Data,
  output [15:0] Address,
  output [3:0] Mask,
  output Finished,
  output Write
);

  wire demultiplexer_2_out1, demultiplexer_3_out1, End, IDLE_q, IncAddr, Load, or_1_out, or_2_out, While_q,
       WriteEnd;
  wire [3:0] counter_1_q;
  wire [31:0] CurrentAddress_q;

  Counter #(.width(32), .max('hffffffff)) CurrentAddress (
    .count(IncAddr), .Q({CurrentAddress_q[31:18], Address, CurrentAddress_q[1:0]}), .clk(Clock), .clr(CLR));  // open: load, D, carry
  or or_1 (or_1_out, IncAddr, demultiplexer_3_out1, Finished);
  D_Flip_Flop IDLE (.clk(Clock), .D(or_1_out), .Q(IDLE_q), .preset(CLR));  // open: Qn, en, reset
  Demultiplexer #(.enable("false")) demultiplexer_1 (.out0(Load), .out1(Finished), .in(IDLE_q), .sel(End));
  D_Flip_Flop While (.clk(Clock), .D(or_2_out), .Q(While_q), .reset(CLR));  // open: Qn, preset, en
  or or_2 (or_2_out, Write, Load);
  RAM_part #(.addrWidth(18), .dataWidth(32)) ram_1 (
    .addr({Address, CurrentAddress_q[1:0]}), .data(Data), .clk(Clock));  // open: sel, ld, clr
  Demultiplexer #(.enable("false")) demultiplexer_2 (
    .out0(Write), .out1(demultiplexer_2_out1), .in(While_q), .sel(WriteEnd));
  Decoder #(.select(2)) decoder_1 (
    .out0(Mask[0]), .out1(Mask[1]), .out2(Mask[2]), .out3(Mask[3]), .sel(CurrentAddress_q[1:0]));  // open: en
  Demultiplexer #(.enable("false")) demultiplexer_3 (
    .out0(IncAddr), .out1(demultiplexer_3_out1), .in(demultiplexer_2_out1), .sel(End));
  Counter #(.width(4), .max('hf)) counter_1 (
    .load(Load), .D(WriteTime), .count(Write), .Q(counter_1_q), .clk(Clock));  // open: carry, clr
  Comparator #(.width(32)) comparator_1 (.a(Data), .b({32{1'b1}}), .eq(End));  // open: gt, lt
  Comparator #(.width(4)) comparator_2 (.a(4'b0000), .b(counter_1_q), .eq(WriteEnd));  // open: gt, lt

  // Other names for the same wires on the sheet: CLK = Clock; Count = Write; WT[3:0] = WriteTime
endmodule

module Register_File (
  input  [4:0] DA,
  input  [31:0] ALU,
  input  R_W,
  input  [31:0] Inst,
  input  [4:0] SA,
  input  [31:0] HI,
  input  [4:0] SB,
  input  Clk,
  input  [31:0] LO,
  input  Clk_2,
  input  Reset,
  input  Random,
  input  Pop,
  input  Push,
  input  lw,
  input  mfhi,
  input  mflo,
  input  rnd,
  input  kbd,
  input  [6:0] Kbd_ASCII_Data,
  output [31:0] A,
  output [31:0] B,
  output [31:0] SP
);

  wire L31, or_4_out, or_5_out, R0, R1, R2, R3, R4, R5, R6, R7, R8, R9, R10, R11, R12, R13, R14, R15, R16,
       R17, R18, R19, R20, R21, R22, R23, R24, R25, R26, R27, R28, R29, R30, R31;
  wire [2:0] selector;
  wire [31:0] adder_1_out, D0, D1, D2, D3, D4, D5, D6, D7, D8, D9, D10, D11, D12, D13, D14, D15, D16, D17,
       D18, D19, D20, D21, D22, D23, D24, D25, D26, D27, D28, D29, D30, Di, KBD_DATA, multiplexer_4_out,
       multiplexer_5_out, RND_t, SP_t, subtractor_1_out;

  Demultiplexer #(.select(5)) demultiplexer_1 (
    .out0(R0), .out1(R1), .out2(R2), .out3(R3), .out4(R4), .out5(R5), .out6(R6), .out7(R7), .out8(R8),
    .out9(R9), .out10(R10), .out11(R11), .out12(R12), .out13(R13), .out14(R14), .out15(R15), .out16(R16),
    .out17(R17), .out18(R18), .out19(R19), .out20(R20), .out21(R21), .out22(R22), .out23(R23), .out24(R24),
    .out25(R25), .out26(R26), .out27(R27), .out28(R28), .out29(R29), .out30(R30), .out31(R31), .in(R_W),
    .sel(DA));  // open: en
  // Probe on SA
  // Probe on SB
  Random #(.width(32)) random_1 (.clk(Clk), .next(1'b1), .out(RND_t));  // open: clr
  // Probe on DA
  assign KBD_DATA = {{25{1'b0}}, Kbd_ASCII_Data};  // Bit_Extender bit_extender_1
  or or_1 (selector[0], lw, Pop, mflo, kbd);
  or or_2 (selector[1], mfhi, mflo);
  or or_3 (selector[2], rnd, kbd);
  // Probe on Inst
  Register #(.width(32)) u_R0 (.D({32{1'b0}}), .en(R0), .Q(D0), .clk(Clk), .clr(Reset));
  Register #(.width(32)) u_R4 (.D(Di), .en(R4), .Q(D4), .clk(Clk), .clr(Reset));
  Register #(.width(32)) u_R8 (.D(Di), .en(R8), .Q(D8), .clk(Clk), .clr(Reset));
  Register #(.width(32)) u_R12 (.D(Di), .en(R12), .Q(D12), .clk(Clk), .clr(Reset));
  Register #(.width(32)) u_R16 (.D(Di), .en(R16), .Q(D16), .clk(Clk), .clr(Reset));
  Register #(.width(32)) u_R20 (.D(Di), .en(R20), .Q(D20), .clk(Clk), .clr(Reset));
  Register #(.width(32)) u_R24 (.D(Di), .en(R24), .Q(D24), .clk(Clk), .clr(Reset));
  Register #(.width(32)) u_R28 (.D(Di), .en(R28), .Q(D28), .clk(Clk), .clr(Reset));
  Multiplexer #(.select(5), .width(32)) multiplexer_1 (
    .in0(D0), .in1(D1), .in2(D2), .in3(D3), .in4(D4), .in5(D5), .in6(D6), .in7(D7), .in8(D8), .in9(D9),
    .in10(D10), .in11(D11), .in12(D12), .in13(D13), .in14(D14), .in15(D15), .in16(D16), .in17(D17),
    .in18(D18), .in19(D19), .in20(D20), .in21(D21), .in22(D22), .in23(D23), .in24(D24), .in25(D25),
    .in26(D26), .in27(D27), .in28(D28), .in29(D29), .in30(D30), .in31(SP), .out(A), .sel(SA));  // open: en
  Multiplexer #(.select(3), .width(32), .enable("false")) multiplexer_2 (
    .in0(ALU), .in1(Inst), .in2(HI), .in3(LO), .in4(RND_t), .in5(KBD_DATA), .out(Di), .sel(selector));  // open: in6, in7
  Register #(.width(32)) u_R1 (.D(Di), .en(R1), .Q(D1), .clk(Clk), .clr(Reset));
  Register #(.width(32)) u_R5 (.D(Di), .en(R5), .Q(D5), .clk(Clk), .clr(Reset));
  Register #(.width(32)) u_R9 (.D(Di), .en(R9), .Q(D9), .clk(Clk), .clr(Reset));
  Register #(.width(32)) u_R13 (.D(Di), .en(R13), .Q(D13), .clk(Clk), .clr(Reset));
  Register #(.width(32)) u_R17 (.D(Di), .en(R17), .Q(D17), .clk(Clk), .clr(Reset));
  Register #(.width(32)) u_R21 (.D(Di), .en(R21), .Q(D21), .clk(Clk), .clr(Reset));
  Register #(.width(32)) u_R25 (.D(Di), .en(R25), .Q(D25), .clk(Clk), .clr(Reset));
  Register #(.width(32)) u_R29 (.D(Di), .en(R29), .Q(D29), .clk(Clk), .clr(Reset));
  // Probe on Di
  Register #(.width(32)) u_R2 (.D(Di), .en(R2), .Q(D2), .clk(Clk), .clr(Reset));
  Register #(.width(32)) u_R6 (.D(Di), .en(R6), .Q(D6), .clk(Clk), .clr(Reset));
  Register #(.width(32)) u_R10 (.D(Di), .en(R10), .Q(D10), .clk(Clk), .clr(Reset));
  Register #(.width(32)) u_R14 (.D(Di), .en(R14), .Q(D14), .clk(Clk), .clr(Reset));
  Register #(.width(32)) u_R18 (.D(Di), .en(R18), .Q(D18), .clk(Clk), .clr(Reset));
  Register #(.width(32)) u_R22 (.D(Di), .en(R22), .Q(D22), .clk(Clk), .clr(Reset));
  Register #(.width(32)) u_R26 (.D(Di), .en(R26), .Q(D26), .clk(Clk), .clr(Reset));
  Register #(.width(32)) u_R30 (.D(Di), .en(R30), .Q(D30), .clk(Clk), .clr(Reset));
  Register #(.width(32)) u_R3 (.D(Di), .en(R3), .Q(D3), .clk(Clk), .clr(Reset));
  Register #(.width(32)) u_R7 (.D(Di), .en(R7), .Q(D7), .clk(Clk), .clr(Reset));
  Register #(.width(32)) u_R11 (.D(Di), .en(R11), .Q(D11), .clk(Clk), .clr(Reset));
  Register #(.width(32)) u_R15 (.D(Di), .en(R15), .Q(D15), .clk(Clk), .clr(Reset));
  Register #(.width(32)) u_R19 (.D(Di), .en(R19), .Q(D19), .clk(Clk), .clr(Reset));
  Register #(.width(32)) u_R23 (.D(Di), .en(R23), .Q(D23), .clk(Clk), .clr(Reset));
  Register #(.width(32)) u_R27 (.D(Di), .en(R27), .Q(D27), .clk(Clk), .clr(Reset));
  Subtractor #(.width(32)) subtractor_1 (.a(SP), .b(32'h4), .out(subtractor_1_out));  // open: bin, bout
  Adder #(.width(32)) adder_1 (.a(32'h4), .b(SP), .out(adder_1_out));  // open: cin, cout
  or or_4 (or_4_out, Push, Pop);
  Multiplexer #(.select(5), .width(32)) multiplexer_3 (
    .in0(D0), .in1(D1), .in2(D2), .in3(D3), .in4(D4), .in5(D5), .in6(D6), .in7(D7), .in8(D8), .in9(D9),
    .in10(D10), .in11(D11), .in12(D12), .in13(D13), .in14(D14), .in15(D15), .in16(D16), .in17(D17),
    .in18(D18), .in19(D19), .in20(D20), .in21(D21), .in22(D22), .in23(D23), .in24(D24), .in25(D25),
    .in26(D26), .in27(D27), .in28(D28), .in29(D29), .in30(D30), .in31(SP), .out(B), .sel(SB));  // open: en
  Multiplexer #(.width(32), .enable("false")) multiplexer_4 (.in0(SP_t), .in1(Di), .out(multiplexer_4_out), .sel(R31));
  Multiplexer #(.width(32), .enable("false")) multiplexer_5 (
    .in0(subtractor_1_out), .in1(adder_1_out), .out(multiplexer_5_out), .sel(Pop));
  and and_1 (L31, Clk_2, or_4_out);
  // Probe on A
  // Probe on B
  Register #(.width(32)) u_R31 (.D(multiplexer_4_out), .en(or_5_out), .Q(SP), .clk(Clk));  // open: clr
  or or_5 (or_5_out, L31, R31, Reset);
  Multiplexer #(.width(32), .enable("false")) multiplexer_6 (
    .in0(multiplexer_5_out), .in1({32{1'b1}}), .out(SP_t), .sel(Reset));

  // Other names for the same wires on the sheet: D31[31:0] = SP; Data_A[31:0] = A; Data_B[31:0] = B;
  //   Instr[31:0] = Inst; is_kbd = kbd; is_rnd = rnd; Mem_RW = Clk_2; Rnd_t_t = Random; RS = Reset

  // Notes on the sheet:
  //   Inputs
  //   Data Address
  //   Read/Write
  //   Selector A
  //   Selector B
  //   Registers
  //   Outputs
  //   Data A
  //   Data B
endmodule

module ALU (
  input  [31:0] A,
  input  [31:0] B,
  input  [3:0] Operation,
  input  M_D,
  input  [31:0] SP,
  input  in_6,
  output [31:0] R,
  output [31:0] HI,
  output [31:0] LO
);

  wire comparator_1_lt, comparator_2_lt;
  wire [3:0] divider_2_out;
  wire [31:0] add, \and , div, high, Mod, mod_t, mult, \nor , \or , Signed_Current, Signed_Div, Signed_Mult,
       slt, sltu, sub, Unsigned_Current, Unsigned_Div, Unsigned_Mult, \xor ;

  // Probe on A
  // Probe on B
  assign \and  = A & B;  // AND_Gate and_1, 32 bits wide
  assign \or  = A | B;  // OR_Gate or_1, 32 bits wide
  Adder #(.width(32)) adder_1 (.a(A), .b(B), .out(add));  // open: cin, cout
  Subtractor #(.width(32)) subtractor_1 (.a(A), .b(B), .out(sub));  // open: bin, bout
  Multiplier #(.width(32)) multiplier_1 (.a(A), .b(B), .out(mult));  // open: cin, cout
  Divider #(.width(32)) divider_1 (.a(A), .b(B), .out(div), .rem(mod_t));  // open: upper
  assign \nor  = ~(A | B);  // NOR_Gate nor_1, 32 bits wide
  assign \xor  = A ^ B;  // XOR_Gate xor_1, 32 bits wide
  Comparator #(.width(32)) comparator_1 (.a(A), .b(B), .lt(comparator_1_lt));  // open: gt, eq
  assign slt = {{31{1'b0}}, comparator_1_lt};  // Bit_Extender bit_extender_1
  Comparator #(.width(32), .mode("unsigned")) comparator_2 (.a(A), .b(B), .lt(comparator_2_lt));  // open: gt, eq
  assign sltu = {{31{1'b0}}, comparator_2_lt};  // Bit_Extender bit_extender_2
  Mult mult_1 (
    .A(A), .B(B), .Output(Unsigned_Mult), .Output_2(Signed_Mult), .Output_3(Unsigned_Current),
    .Output_4(Signed_Current));
  Div div_1 (.A(A), .B(B), .Mod(Mod), .Output(Unsigned_Div), .Output_2(Signed_Div));
  Divider #(.width(4)) divider_2 (.a(Operation), .b(4'b0010), .out(divider_2_out));  // open: upper, rem
  Multiplexer #(.select(4), .width(32)) multiplexer_1 (
    .in0(add), .in1(sub), .in2(Signed_Mult), .in3(Unsigned_Mult), .in4(Unsigned_Div), .in5(Signed_Div),
    .in6(\and ), .in7(\or ), .in8(\nor ), .in9(\xor ), .in10(slt), .in11(sltu), .in15({32{1'b0}}), .out(R),
    .sel(Operation));  // open: in12, in13, in14, en
  Multiplexer #(.select(2), .width(32), .enable("false")) multiplexer_2 (
    .in0(Unsigned_Current), .in1(Signed_Current), .in2(Mod), .in3(Mod), .out(high), .sel(divider_2_out[1:0]));
  // Probe on R
  Register #(.width(32)) u_High (.D(high), .en(M_D), .Q(HI), .clk(in_6));  // open: clr
  Register #(.width(32)) Low (.D(R), .en(M_D), .Q(LO), .clk(in_6));  // open: clr

  // Other names for the same wires on the sheet: Clk = in_6; low[31:0] = R; Op[3:0] = Operation
endmodule

module Mult (
  input  [31:0] A,
  input  [31:0] B,
  output [31:0] Output,
  output [31:0] Output_2,
  output [31:0] Output_3,
  output [31:0] Output_4
);

  wire [31:0] a_denied, b_denied, multiplexer_1_out, multiplexer_2_out, not_1_out, not_2_out;

  assign not_1_out = ~A;  // NOT_Gate not_1, 32 bits wide
  Adder #(.width(32)) adder_1 (.a(not_1_out), .b(32'h1), .out(a_denied));  // open: cin, cout
  assign not_2_out = ~B;  // NOT_Gate not_2, 32 bits wide
  Adder #(.width(32)) adder_2 (.a(not_2_out), .b(32'h1), .out(b_denied));  // open: cin, cout
  Multiplexer #(.width(32)) multiplexer_1 (.in0(A), .in1(a_denied), .out(multiplexer_1_out), .sel(A[31]));  // open: en
  Multiplexer #(.width(32)) multiplexer_2 (.in0(B), .in1(b_denied), .out(multiplexer_2_out), .sel(B[31]));  // open: en
  Multiplier #(.width(32)) multiplier_1 (.a(A), .b(B), .out(Output_2), .cin({32{1'b0}}), .cout(Output_4));
  Multiplier #(.width(32)) multiplier_2 (
    .a(multiplexer_1_out), .b(multiplexer_2_out), .out(Output), .cin({32{1'b0}}), .cout(Output_3));

  // Other names for the same wires on the sheet: a_sign = A[31]; b_sign = B[31]; Signed_current[31:0] = Output_4;
  //   Signed_multiply[31:0] = Output_2; Unsigned_current[31:0] = Output_3; Unsigned_multiply[31:0] = Output

  // Notes on the sheet:
  //   Negate Inputs
endmodule

module Div (
  input  [31:0] A,
  input  [31:0] B,
  output [31:0] Output,
  output [31:0] Mod,
  output [31:0] Output_2
);

  wire [31:0] a_denied, b_denied, multiplexer_1_out, multiplexer_2_out, not_1_out, not_2_out;

  assign not_1_out = ~A;  // NOT_Gate not_1, 32 bits wide
  Adder #(.width(32)) adder_1 (.a(not_1_out), .b(32'h1), .out(a_denied));  // open: cin, cout
  assign not_2_out = ~B;  // NOT_Gate not_2, 32 bits wide
  Adder #(.width(32)) adder_2 (.a(not_2_out), .b(32'h1), .out(b_denied));  // open: cin, cout
  Multiplexer #(.width(32)) multiplexer_1 (.in0(A), .in1(a_denied), .out(multiplexer_1_out), .sel(A[31]));  // open: en
  Multiplexer #(.width(32)) multiplexer_2 (.in0(B), .in1(b_denied), .out(multiplexer_2_out), .sel(B[31]));  // open: en
  Divider #(.width(32)) divider_1 (.a(A), .b(B), .out(Output_2), .upper({32{1'b0}}));  // open: rem
  Divider #(.width(32)) divider_2 (
    .a(multiplexer_1_out), .b(multiplexer_2_out), .out(Output), .upper({32{1'b0}}), .rem(Mod));

  // Other names for the same wires on the sheet: a_sign = A[31]; b_sign = B[31]; Signed_div[31:0] = Output_2;
  //   Unsigned_div[31:0] = Output

  // Notes on the sheet:
  //   Negate Inputs
endmodule

module Instruction_Decoder (
  input  [31:0] Instruction,
  output [4:0] Data_Address,
  output [4:0] Sa,
  output [4:0] Sb,
  output [25:0] Destino_Salto,
  output Mult_Div,
  output R_W,
  output [31:0] K,
  output Tipo_I,
  output Output,
  output [3:0] Selector_Alu,
  output [2:0] Selector_Branch,
  output jmp,
  output Output_2,
  output Output_3,
  output Output_4,
  output Output_5,
  output Output_6,
  output Output_7,
  output Output_8,
  output Output_9,
  output Output_10,
  output Output_11,
  output Output_12,
  output ALU_instr,
  output Output_13,
  output Output_14
);

  wire add, addi, \and , andi, beq, bgtz, blez, bltz, bne, comparator_18_eq, comparator_19_eq,
       comparator_20_eq, comparator_21_eq, comparator_22_eq, comparator_23_eq, comparator_24_eq,
       comparator_25_eq, comparator_26_eq, comparator_27_eq, comparator_28_eq, comparator_29_eq,
       comparator_30_eq, comparator_31_eq, comparator_32_eq, comparator_33_eq, comparator_34_eq,
       comparator_35_eq, comparator_36_eq, comparator_37_eq, comparator_38_eq, comparator_39_eq, div, divu,
       j, jr, mult, mulu, nop, \nor , oper, \or , or_1_out, or_2_out, or_3_out, or_4_out, or_5_out, or_6_out,
       or_7_out, or_8_out, or_9_out, or_10_out, or_11_out, or_12_out, ori, slt, slti, sltiu, sltu, special,
       sub, Tipo_R, \xor , xori;

  // Probe on Instruction[31:26]
  or or_1 (or_1_out, \and , andi);
  Comparator #(.width(6)) comparator_1 (.a(Instruction[31:26]), .b({6{1'b0}}), .eq(oper));  // open: gt, lt
  Comparator #(.width(6)) comparator_2 (.a(Instruction[31:26]), .b(6'b111000), .eq(Output_13));  // open: gt, lt
  Comparator #(.width(6)) comparator_3 (.a(Instruction[31:26]), .b({6{1'b1}}), .eq(special));  // open: gt, lt
  Comparator #(.width(6)) comparator_4 (.a(Instruction[31:26]), .b(6'b001000), .eq(addi));  // open: gt, lt
  Comparator #(.width(6)) comparator_5 (.a(Instruction[31:26]), .b(6'b001100), .eq(andi));  // open: gt, lt
  Comparator #(.width(6)) comparator_6 (.a(Instruction[31:26]), .b(6'b001101), .eq(ori));  // open: gt, lt
  Comparator #(.width(6)) comparator_7 (.a(Instruction[31:26]), .b(6'b001110), .eq(xori));  // open: gt, lt
  Comparator #(.width(6)) comparator_8 (.a(Instruction[31:26]), .b(6'b001010), .eq(slti));  // open: gt, lt
  Comparator #(.width(6)) comparator_9 (.a(Instruction[31:26]), .b(6'b001011), .eq(sltiu));  // open: gt, lt
  Comparator #(.width(6)) comparator_10 (.a(Instruction[31:26]), .b(6'b000100), .eq(beq));  // open: gt, lt
  Comparator #(.width(6)) comparator_11 (.a(Instruction[31:26]), .b(6'b000101), .eq(bne));  // open: gt, lt
  Comparator #(.width(6)) comparator_12 (.a(Instruction[31:26]), .b(6'b000110), .eq(blez));  // open: gt, lt
  Comparator #(.width(6)) comparator_13 (.a(Instruction[31:26]), .b(6'b000111), .eq(bgtz));  // open: gt, lt
  Comparator #(.width(6)) comparator_14 (.a(Instruction[31:26]), .b(6'b000001), .eq(bltz));  // open: gt, lt
  Comparator #(.width(6)) comparator_15 (.a(Instruction[31:26]), .b(6'b100011), .eq(Output_10));  // open: gt, lt
  Comparator #(.width(6)) comparator_16 (.a(Instruction[31:26]), .b(6'b101011), .eq(Output_11));  // open: gt, lt
  Comparator #(.width(6)) comparator_17 (.a(Instruction[31:26]), .b(6'b000010), .eq(j));  // open: gt, lt
  or or_2 (or_2_out, add, addi, Output_10, Output_11);
  or or_3 (or_3_out, \or , ori);
  or or_4 (or_4_out, \xor , xori);
  or or_5 (or_5_out, slt, slti);
  or or_6 (or_6_out, sltu, sltiu);
  or or_7 (or_7_out, add, addi);
  or or_8 (or_8_out, \and , andi);
  or or_9 (or_9_out, \or , ori);
  or or_10 (or_10_out, \xor , xori);
  or or_11 (or_11_out, slt, slti);
  or or_12 (or_12_out, sltu, sltiu);
  // Probe on Instruction[25:21]
  or or_13 (Tipo_R, oper, Output_13, special);
  or or_14 (Tipo_I, addi, andi, ori, xori, slti, sltiu, beq, bne, blez, bgtz, bltz, Output_10, Output_11);
  or or_15 (ALU_instr, or_7_out, sub, mult, mulu, div, divu, or_8_out, or_9_out, or_10_out, or_11_out, or_12_out, Output_8, Output_9, \nor );
  Operation_Alu operation_alu_1 (
    .Addition(or_2_out), .Substract(sub), .Multiply(mult), .Unsigned_Multiply(mulu), .Divide(div),
    .Unsigned_Divide(divu), .Logical_And(or_1_out), .Logical_Or(or_3_out), .Logical_Nor(\nor ),
    .Logical_Xor(or_4_out), .Set_less_than(or_5_out), .Unsigned_set_less_than(or_6_out),
    .Selector_Alu(Selector_Alu), .Move_from_Hi(Output_8), .Move_from_Lo(Output_9));  // open: ALU
  // Probe on Instruction[15:0]
  // Probe on Instruction[5:0]
  // Probe on Instruction
  Comparator #(.width(6)) comparator_18 (.a(Instruction[5:0]), .b(6'b100000), .eq(comparator_18_eq));  // open: gt, lt
  Comparator #(.width(6)) comparator_19 (.a(Instruction[5:0]), .b(6'b100010), .eq(comparator_19_eq));  // open: gt, lt
  Comparator #(.width(6)) comparator_20 (.a(Instruction[5:0]), .b(6'b011000), .eq(comparator_20_eq));  // open: gt, lt
  Comparator #(.width(6)) comparator_21 (.a(Instruction[5:0]), .b(6'b011001), .eq(comparator_21_eq));  // open: gt, lt
  Comparator #(.width(6)) comparator_22 (.a(Instruction[5:0]), .b(6'b011010), .eq(comparator_22_eq));  // open: gt, lt
  Comparator #(.width(6)) comparator_23 (.a(Instruction[5:0]), .b(6'b011011), .eq(comparator_23_eq));  // open: gt, lt
  Comparator #(.width(6)) comparator_24 (.a(Instruction[5:0]), .b(6'b100100), .eq(comparator_24_eq));  // open: gt, lt
  Comparator #(.width(6)) comparator_25 (.a(Instruction[5:0]), .b(6'b100101), .eq(comparator_25_eq));  // open: gt, lt
  Comparator #(.width(6)) comparator_26 (.a(Instruction[5:0]), .b(6'b100111), .eq(comparator_26_eq));  // open: gt, lt
  Comparator #(.width(6)) comparator_27 (.a(Instruction[5:0]), .b(6'b101000), .eq(comparator_27_eq));  // open: gt, lt
  Comparator #(.width(6)) comparator_28 (.a(Instruction[5:0]), .b(6'b101010), .eq(comparator_28_eq));  // open: gt, lt
  Comparator #(.width(6)) comparator_29 (.a(Instruction[5:0]), .b(6'b101011), .eq(comparator_29_eq));  // open: gt, lt
  Comparator #(.width(6)) comparator_30 (.a(Instruction[5:0]), .b(6'b010000), .eq(comparator_30_eq));  // open: gt, lt
  Comparator #(.width(6)) comparator_31 (.a(Instruction[5:0]), .b(6'b010010), .eq(comparator_31_eq));  // open: gt, lt
  Comparator #(.width(6)) comparator_32 (.a(Instruction[5:0]), .b({6{1'b0}}), .eq(comparator_32_eq));  // open: gt, lt
  Comparator #(.width(6)) comparator_33 (.a(Instruction[5:0]), .b(6'b001000), .eq(comparator_33_eq));  // open: gt, lt
  Comparator #(.width(6)) comparator_34 (.a(Instruction[5:0]), .b({6{1'b0}}), .eq(comparator_34_eq));  // open: gt, lt
  Comparator #(.width(6)) comparator_35 (.a(Instruction[5:0]), .b(6'b000001), .eq(comparator_35_eq));  // open: gt, lt
  Comparator #(.width(6)) comparator_36 (.a(Instruction[5:0]), .b({6{1'b1}}), .eq(comparator_36_eq));  // open: gt, lt
  Comparator #(.width(6)) comparator_37 (.a(Instruction[5:0]), .b(6'b000001), .eq(comparator_37_eq));  // open: gt, lt
  Comparator #(.width(6)) comparator_38 (.a(Instruction[5:0]), .b(6'b000010), .eq(comparator_38_eq));  // open: gt, lt
  Comparator #(.width(6)) comparator_39 (.a(Instruction[5:0]), .b(6'b000100), .eq(comparator_39_eq));  // open: gt, lt
  or or_16 (Output_12, Output_11, Output_10);
  or or_17 (Output_14, Output_11, Output_3);
  and and_1 (add, Tipo_R, comparator_18_eq);
  and and_2 (sub, Tipo_R, comparator_19_eq);
  and and_3 (mult, Tipo_R, comparator_20_eq);
  and and_4 (mulu, Tipo_R, comparator_21_eq);
  and and_5 (div, Tipo_R, comparator_22_eq);
  and and_6 (divu, Tipo_R, comparator_23_eq);
  and and_7 (\and , Tipo_R, comparator_24_eq);
  and and_8 (\or , Tipo_R, comparator_25_eq);
  and and_9 (\nor , Tipo_R, comparator_26_eq);
  and and_10 (\xor , Tipo_R, comparator_27_eq);
  and and_11 (slt, Tipo_R, comparator_28_eq);
  and and_12 (sltu, Tipo_R, comparator_29_eq);
  and and_13 (Output_8, Tipo_R, comparator_30_eq);
  and and_14 (Output_9, Tipo_R, comparator_31_eq);
  and and_15 (jr, Tipo_R, comparator_33_eq);
  and and_16 (Output_2, Output_13, comparator_34_eq);
  and and_17 (Output_3, Output_13, comparator_35_eq);
  and and_18 (Output_4, special, comparator_36_eq);
  and and_19 (Output_5, special, comparator_37_eq);
  and and_20 (Output_6, special, comparator_38_eq);
  and and_21 (Output_7, special, comparator_39_eq);
  or or_18 (Output, Output_6, Output_9, Output_7, Output_8, Output_5);
  and and_22 (nop, oper, comparator_32_eq);
  Multiplexer #(.width(5), .enable("false")) multiplexer_1 (
    .in0(Instruction[25:21]), .in1(Instruction[20:16]), .out(Sa), .sel(1'b0));
  Multiplexer #(.width(5), .enable("false")) multiplexer_2 (
    .in0(Instruction[20:16]), .in1(Instruction[25:21]), .out(Sb), .sel(1'b0));
  Multiplexer #(.width(5)) multiplexer_3 (
    .in0(Instruction[15:11]), .in1(Instruction[20:16]), .out(Data_Address), .sel(Tipo_I), .en(1'b1));
  or or_19 (Mult_Div, mult, mulu, div, divu);
  Branch_Jump branch_jump_1 (
    .Branch_on_equal(beq), .Branch_on_not_equal(bne), .Branch_on_less_than_or_equal_zero(blez),
    .Branch_on_greater_than_zero(bgtz), .Branch_on_less_than_zero(bltz), .Jump(j), .Jump_register(jr),
    .Branch_Selector(Selector_Branch));
  or or_20 (jmp, jr, j, bltz, bgtz, blez, bne, beq, nop);
  or or_21 (R_W, add, sub, \and , \or , \nor , \xor , slt, sltu, Output_8, Output_9, Output_2, Output_6, addi, andi, ori, xori, slti, sltiu, Output_10);
  assign K = {{16{Instruction[15]}}, Instruction[15:0]};  // Bit_Extender bit_extender_1

  assign Destino_Salto = Instruction[25:0];

  // Other names for the same wires on the sheet: halt = Output_4; Constante[15:0] = Instruction[15:0];
  //   Func_code[5:0] = Instruction[5:0]; Rd[4:0] = Instruction[15:11]; Rt[4:0] = Instruction[20:16];
  //   Rs[4:0] = Instruction[25:21]; Op_code[5:0] = Instruction[31:26]; Tipo_J = j; kbd = Output_7; lw = Output_10;
  //   mem_inst = Output_12; mfhi = Output_8; mflo = Output_9; pop = Output_2; push = Output_3; R = Output;
  //   rnd = Output_6; stack = Output_13; sw = Output_11; tty = Output_5; write_inst = Output_14

  // Notes on the sheet:
  //   Formato R
  //   Formato I
  //   Instrucciones tipo R
  //   Formato J
  //   Outputs
endmodule

module Operation_Alu (
  input  Addition,
  input  Substract,
  input  Multiply,
  input  Unsigned_Multiply,
  input  Divide,
  input  Unsigned_Divide,
  input  Logical_And,
  input  Logical_Or,
  input  Logical_Nor,
  input  Logical_Xor,
  input  Set_less_than,
  input  Unsigned_set_less_than,
  input  Move_from_Hi,
  input  Move_from_Lo,
  output [3:0] Selector_Alu,
  output ALU
);

  wire not_1_out, not_2_out, not_3_out, not_4_out, not_5_out, not_6_out, not_7_out, not_8_out, not_9_out,
       not_10_out, not_11_out, not_12_out, not_13_out, not_14_out, not_15_out, not_16_out, not_17_out,
       not_18_out, not_19_out, not_20_out, not_21_out, not_22_out, not_23_out, not_24_out, not_25_out,
       not_26_out, not_27_out, not_28_out, not_29_out, not_30_out, not_31_out;

  not not_1 (not_1_out, Addition);
  not not_2 (not_2_out, Multiply);
  not not_3 (not_3_out, Divide);
  not not_4 (not_4_out, Logical_And);
  not not_5 (not_5_out, Logical_Nor);
  not not_6 (not_6_out, Set_less_than);
  not not_7 (not_7_out, Move_from_Hi);
  not not_8 (not_8_out, Addition);
  not not_9 (not_9_out, Substract);
  not not_10 (not_10_out, Divide);
  not not_11 (not_11_out, Unsigned_Divide);
  not not_12 (not_12_out, Logical_Nor);
  not not_13 (not_13_out, Logical_Xor);
  not not_14 (not_14_out, Move_from_Hi);
  not not_15 (not_15_out, Move_from_Lo);
  and and_1 (Selector_Alu[0], not_1_out, not_2_out, not_3_out, not_4_out, not_5_out, not_6_out, not_7_out);
  and and_2 (Selector_Alu[1], not_8_out, not_9_out, not_10_out, not_11_out, not_12_out, not_13_out, not_14_out, not_15_out);
  not not_16 (not_16_out, Addition);
  not not_17 (not_17_out, Substract);
  not not_18 (not_18_out, Addition);
  not not_19 (not_19_out, Substract);
  not not_20 (not_20_out, Multiply);
  not not_21 (not_21_out, Unsigned_Multiply);
  not not_22 (not_22_out, Divide);
  not not_23 (not_23_out, Unsigned_Divide);
  not not_24 (not_24_out, Logical_And);
  not not_25 (not_25_out, Logical_Or);
  not not_26 (not_26_out, Multiply);
  not not_27 (not_27_out, Unsigned_Multiply);
  not not_28 (not_28_out, Logical_Nor);
  not not_29 (not_29_out, Logical_Xor);
  not not_30 (not_30_out, Set_less_than);
  not not_31 (not_31_out, Unsigned_set_less_than);
  and and_3 (Selector_Alu[2], not_16_out, not_17_out, not_26_out, not_27_out, not_28_out, not_29_out, not_30_out, not_31_out);
  and and_4 (Selector_Alu[3], not_18_out, not_19_out, not_20_out, not_21_out, not_22_out, not_23_out, not_24_out, not_25_out);
  or or_1 (ALU, Addition, Substract, Multiply, Unsigned_Multiply, Divide, Unsigned_Divide, Logical_And, Logical_Or, Logical_Nor, Logical_Xor, Set_less_than, Unsigned_set_less_than, Move_from_Hi, Move_from_Lo);

  // Other names for the same wires on the sheet: add = Addition; and = Logical_And; mfhi = Move_from_Hi;
  //   mflo = Move_from_Lo; nor = Logical_Nor; or = Logical_Or; Bit_1 = Selector_Alu[0]; Bit_2 = Selector_Alu[1];
  //   Bit_3 = Selector_Alu[2]; Bit_4 = Selector_Alu[3]; Signed_Div = Unsigned_Divide; Signed_Mult = Multiply;
  //   slt = Set_less_than; sltu = Unsigned_set_less_than; sub = Substract; Unsigned_Div = Divide;
  //   Unsigned_Mult = Unsigned_Multiply; xor = Logical_Xor
endmodule

module Data_Path (
  input  [31:0] in_1,
  input  Reset,
  input  Clock,
  input  En_Get_Inst,
  input  Is_PC,
  input  En_PC,
  input  [6:0] Kbd_ASCII_Data,
  input  in_8,
  output [31:0] Output,
  output [31:0] R,
  output jmp,
  output ALU_inst,
  output Memorie_Inst,
  output Stack_inst,
  output Write_inst,
  output R_instr,
  output stop,
  output tty_en,
  output [6:0] Output_2
);

  wire Inmediate, KBD_ENABLE, lw, mfhi, mflo, Mult_Div, or_1_out, pop, push, Read_Write, Rnd, sw;
  wire [2:0] Sb;
  wire [3:0] Operation;
  wire [4:0] Data_Address, Selector_A, Selector_B;
  wire [25:0] Destino_Salto;
  wire [31:0] B, Constant, HI, IA_prime, instruction_register_1_output, LO, multiplexer_1_out, PC, Result, SP;
  wire [31:7] A;

  Branch_Control Branch_Control (
    .in_1(jmp), .Output(IA_prime), .in_4(PC), .in_2({A, Output_2}), .in_3(B), .in_6(Sb),
    .in_5(Destino_Salto), .in_7(Constant));
  Instruction_Register instruction_register_1 (
    .Instruction(in_1), .Output(instruction_register_1_output), .in_2(Reset), .in_3(Clock), .in_4(En_Get_Inst));  // open: Instruction_Charged
  Register_File Register_File (
    .DA(Data_Address), .A({A, Output_2}), .B(B), .R_W(in_8), .SA(Selector_A), .SB(Selector_B), .Reset(Clock),
    .Pop(pop), .Push(push), .Clk(Reset), .Random(Rnd), .Kbd_ASCII_Data(Kbd_ASCII_Data), .SP(SP),
    .ALU(Result), .Inst(in_1), .HI(HI), .LO(LO), .lw(lw), .mfhi(mfhi), .mflo(mflo), .rnd(Rnd),
    .kbd(KBD_ENABLE), .Clk_2(En_PC));
  Program_Counter Program_Counter (.Input(IA_prime), .Clock(Reset), .Enable(En_PC), .Output(PC), .Reset(Clock));
  Instruction_Decoder instruction_decoder_1 (
    .Instruction(instruction_register_1_output), .Data_Address(Data_Address), .Sa(Selector_A),
    .Sb(Selector_B), .Destino_Salto(Destino_Salto), .Mult_Div(Mult_Div), .R_W(Read_Write), .K(Constant),
    .Selector_Alu(Operation), .Tipo_I(Inmediate), .Selector_Branch(Sb), .jmp(jmp), .Output_2(pop),
    .Output_3(push), .Output_4(stop), .Output_5(tty_en), .Output_6(Rnd), .Output_7(KBD_ENABLE),
    .Output_8(mfhi), .Output_9(mflo), .Output_10(lw), .Output_11(sw), .Output_12(Memorie_Inst),
    .Output_13(Stack_inst), .Output_14(Write_inst), .ALU_instr(ALU_inst), .Output(R_instr));
  Memory_Address Memorie_Address (
    .PC(PC), .ALU(Result), .SP(SP), .lw(lw), .sw(sw), .pop(pop), .push(push), .pc_2(Is_PC), .Output(Output));
  ALU ALU (
    .A({A, Output_2}), .B(multiplexer_1_out), .R(Result), .Operation(Operation), .M_D(Mult_Div), .SP(SP),
    .HI(HI), .LO(LO), .in_6(Reset));
  Multiplexer #(.width(32)) multiplexer_1 (
    .in0(B), .in1(Constant), .out(multiplexer_1_out), .sel(Inmediate));  // open: en
  // Probe on Result
  or or_1 (or_1_out, pop, push);
  // Probe on HI
  Multiplexer #(.width(32), .enable("false")) multiplexer_2 (.in0({A, Output_2}), .in1(B), .out(R), .sel(sw));

  // Other names for the same wires on the sheet: A[6:0] = Output_2; ALU_instruction = ALU_inst; CLK = Reset;
  //   CLR = Clock; EGI = En_Get_Inst; Enable_PC = En_PC; Instruction[31:0] = in_1; KBD_DATA[6:0] = Kbd_ASCII_Data;
  //   Memorie_Address[31:0] = Output; Memorie_Instruction = Memorie_Inst; RF_RW = in_8;
  //   Stack_Instruction = Stack_inst; Tipo_R = R_instr; TTY_ENABLE = tty_en; Write_Instruction = Write_inst

  // Notes on the sheet:
  //   Outputs
endmodule

module Program_Counter (
  input  [31:0] Input,
  input  Clock,
  input  Enable,
  input  Reset,
  output [31:0] Output
);

  Register #(.width(32)) register_1 (.D(Input), .en(Enable), .Q(Output), .clk(Clock), .clr(Reset));

  // Other names for the same wires on the sheet: Clck = Clock; Clr = Reset; En = Enable
endmodule

module Branch_Jump (
  input  Branch_on_equal,
  input  Branch_on_not_equal,
  input  Branch_on_less_than_or_equal_zero,
  input  Branch_on_greater_than_zero,
  input  Branch_on_less_than_zero,
  input  Jump,
  input  Jump_register,
  output [2:0] Branch_Selector
);

  wire not_1_out, not_2_out, not_3_out, not_4_out, not_5_out, not_6_out, not_7_out, not_8_out, not_9_out,
       not_10_out, not_11_out, not_12_out;

  not not_1 (not_1_out, Branch_on_equal);
  not not_2 (not_2_out, Branch_on_less_than_or_equal_zero);
  not not_3 (not_3_out, Branch_on_less_than_zero);
  not not_4 (not_4_out, Jump_register);
  not not_5 (not_5_out, Branch_on_equal);
  not not_6 (not_6_out, Branch_on_not_equal);
  not not_7 (not_7_out, Branch_on_less_than_zero);
  not not_8 (not_8_out, Jump);
  not not_9 (not_9_out, Branch_on_equal);
  not not_10 (not_10_out, Branch_on_not_equal);
  not not_11 (not_11_out, Branch_on_less_than_or_equal_zero);
  not not_12 (not_12_out, Branch_on_greater_than_zero);
  and and_1 (Branch_Selector[0], not_1_out, not_2_out, not_3_out, not_4_out);
  and and_2 (Branch_Selector[1], not_5_out, not_6_out, not_7_out, not_8_out);
  and and_3 (Branch_Selector[2], not_9_out, not_10_out, not_11_out, not_12_out);

  // Other names for the same wires on the sheet: beq = Branch_on_equal; bgtz = Branch_on_greater_than_zero;
  //   blez = Branch_on_less_than_or_equal_zero; bltz = Branch_on_less_than_zero; bne = Branch_on_not_equal;
  //   bit_1 = Branch_Selector[0]; bit_2 = Branch_Selector[1]; bit_3 = Branch_Selector[2]; j = Jump;
  //   jr = Jump_register
endmodule

module Control_Unit (
  input  in_1,
  input  in_2,
  input  in_3,
  input  in_4,
  input  in_5,
  input  in_6,
  input  Instrucciones,
  input  in_8,
  input  in_9,
  input  in_10,
  input  in_11,
  input  in_12,
  input  in_13,
  output Read_Inst,
  output Read_Data,
  output Write,
  output Output,
  output En_Get_Inst,
  output Output_2,
  output Output_3,
  output Output_4,
  output Output_5
);

  wire branch, d_ff_1_q, d_ff_2_q, d_ff_3_q, d_ff_4_q, demultiplexer_1_out0, demultiplexer_1_out1, or_5_out,
       RF;
  wire [2:0] or_3_out;

  or or_1 (or_3_out[2], in_9, in_11);
  Demultiplexer #(.select(3), .enable("false")) demultiplexer_1 (
    .out0(demultiplexer_1_out0), .out1(demultiplexer_1_out1), .out2(branch), .out3(RF), .out4(Read_Data),
    .out5(Write), .in(d_ff_1_q), .sel(or_3_out));  // open: out6, out7
  D_Flip_Flop #(.trigger("falling")) d_ff_1 (.clk(in_1), .D(in_4), .Q(d_ff_1_q));  // open: Qn, preset, en, reset
  or or_2 (or_3_out[1], in_8, in_10);
  D_Flip_Flop #(.trigger("falling")) d_ff_2 (
    .clk(in_1), .D(in_2), .Q(d_ff_2_q), .reset(in_13));  // open: Qn, preset, en
  D_Flip_Flop #(.trigger("falling")) d_ff_3 (
    .clk(in_1), .D(Output), .Q(d_ff_3_q), .reset(in_13));  // open: Qn, preset, en
  and and_1 (Output_2, Output_3, in_12);
  or or_3 (or_3_out[0], in_8, Instrucciones, in_11);
  or or_4 (Read_Inst, d_ff_2_q, d_ff_3_q);
  or or_5 (or_5_out, Output_4, demultiplexer_1_out0);
  D_Flip_Flop #(.trigger("falling")) d_ff_4 (
    .clk(in_1), .D(demultiplexer_1_out1), .Q(d_ff_4_q), .reset(in_13));  // open: Qn, preset, en
  D_Flip_Flop #(.trigger("falling")) d_ff_5 (
    .clk(in_1), .D(or_5_out), .Q(Output_4), .reset(in_13));  // open: Qn, preset, en
  or or_6 (Output_5, d_ff_4_q, in_6, RF);
  D_Flip_Flop #(.trigger("falling")) d_ff_6 (.clk(in_1), .D(Output_5), .Q(Output_3));  // open: Qn, preset, en, reset
  or or_7 (Output, Output_3, in_5, branch);

  assign En_Get_Inst = in_4;

  // Other names for the same wires on the sheet: ALU = Instrucciones; Cl = in_1; Cs = in_3; Data = in_6;
  //   En_PC = Output; En_tty = Output_2; Get_Inst = in_2; jmp = in_10; mem = in_9; R = in_8; RData = Read_Data;
  //   Read = Read_Inst; Readed = in_4; reset = in_13; RW = Output_5; stop = Output_4; tty = in_12; En_kbd = Output_3;
  //   tty_ = Output_3; write_inst = in_11; Writen = in_5

  // Notes on the sheet:
  //   Outputs
endmodule

module Instruction_Memory (
  input  [31:0] Address,
  input  [31:0] instruction_block_0,
  input  [31:0] instruction_block_1,
  input  [31:0] instruction_block_2,
  input  [31:0] instruction_block_3,
  input  [3:0] in_6,
  input  Clock,
  input  Reset,
  input  Obtain_Instruction,
  input  Halt,
  output [31:0] output_block_0,
  output [31:0] output_block_1,
  output [31:0] output_block_2,
  output [31:0] output_block_3,
  output Chip_Select,
  output Ready
);

  wire CS1, CS2, or_2_out, timer_1_ready;

  or or_1 (Chip_Select, CS1, CS2);
  or or_2 (or_2_out, Obtain_Instruction, timer_1_ready);
  D_Flip_Flop #(.trigger("falling")) d_ff_1 (
    .clk(Clock), .D(Obtain_Instruction), .Q(CS1), .en(or_2_out));  // open: Qn, preset, reset
  Timer timer_1 (.Time(in_6), .Ready(timer_1_ready), .Clock(Clock), .Reset(Ready), .Start(CS1));
  Register #(.width(32)) register_1 (.D(instruction_block_0), .en(CS2), .Q(output_block_0), .clk(Clock), .clr(Reset));
  Register #(.width(32)) register_2 (.D(instruction_block_1), .en(CS2), .Q(output_block_1), .clk(Clock), .clr(Reset));
  Register #(.width(32)) register_3 (.D(instruction_block_2), .en(CS2), .Q(output_block_2), .clk(Clock), .clr(Reset));
  Register #(.width(32)) register_4 (.D(instruction_block_3), .en(CS2), .Q(output_block_3), .clk(Clock), .clr(Reset));
  D_Flip_Flop #(.trigger("falling")) d_ff_2 (
    .clk(Clock), .D(timer_1_ready), .Q(CS2), .reset(Ready));  // open: Qn, preset, en
  D_Flip_Flop #(.trigger("falling")) d_ff_3 (.clk(Clock), .D(CS2), .Q(Ready));  // open: Qn, preset, en, reset

  // Other names for the same wires on the sheet: Clck = Clock; CS = Chip_Select; Inst_Out_0[31:0] = output_block_0;
  //   Inst_Out_1[31:0] = output_block_1; Inst_Out_2[31:0] = output_block_2; Inst_Out_3[31:0] = output_block_3;
  //   obtain_inst = Obtain_Instruction; RAM_OUTPUT_0[31:0] = instruction_block_0;
  //   RAM_OUTPUT_1[31:0] = instruction_block_1; RAM_OUTPUT_2[31:0] = instruction_block_2;
  //   RAM_OUTPUT_3[31:0] = instruction_block_3; read_time[3:0] = in_6
endmodule

module Data_Memory (
  input  [31:0] Address,
  input  [31:0] data_block_0,
  input  [31:0] data_block_1,
  input  [31:0] data_block_2,
  input  [31:0] data_block_3,
  input  [3:0] in_6,
  input  Clock,
  input  Reset,
  input  Obtain_Data,
  output [31:0] output_block_0,
  output [31:0] output_block_1,
  output [31:0] output_block_2,
  output [31:0] output_block_3,
  output WCS,
  output Ready
);

  wire or_1_out, timer_1_ready, WCS1, WCS2;

  or or_1 (or_1_out, Obtain_Data, timer_1_ready);
  D_Flip_Flop #(.trigger("falling")) d_ff_1 (
    .clk(Clock), .D(Obtain_Data), .Q(WCS1), .en(or_1_out));  // open: Qn, preset, reset
  Timer timer_1 (.Time(in_6), .Ready(timer_1_ready), .Clock(Clock), .Reset(Ready), .Start(WCS1));
  D_Flip_Flop #(.trigger("falling")) d_ff_2 (
    .clk(Clock), .D(timer_1_ready), .Q(WCS2), .reset(Ready));  // open: Qn, preset, en
  Register #(.width(32)) register_1 (.D(data_block_0), .en(WCS2), .Q(output_block_0), .clk(Clock), .clr(Reset));
  Register #(.width(32)) register_2 (.D(data_block_1), .en(WCS2), .Q(output_block_1), .clk(Clock), .clr(Reset));
  Register #(.width(32)) register_3 (.D(data_block_2), .en(WCS2), .Q(output_block_2), .clk(Clock), .clr(Reset));
  Register #(.width(32)) register_4 (.D(data_block_3), .en(WCS2), .Q(output_block_3), .clk(Clock), .clr(Reset));
  D_Flip_Flop #(.trigger("falling")) d_ff_3 (.clk(Clock), .D(WCS2), .Q(Ready));  // open: Qn, preset, en, reset
  or or_2 (WCS, WCS1, WCS2);

  // Other names for the same wires on the sheet: Clck = Clock; Inst_Out_0[31:0] = output_block_0;
  //   Inst_Out_1[31:0] = output_block_1; Inst_Out_2[31:0] = output_block_2; Inst_Out_3[31:0] = output_block_3;
  //   RAM_OUTPUT_0[31:0] = data_block_0; RAM_OUTPUT_1[31:0] = data_block_1; RAM_OUTPUT_2[31:0] = data_block_2;
  //   RAM_OUTPUT_3[31:0] = data_block_3; Ready_Write = Ready; write_time[3:0] = in_6
endmodule

module Branch_Control (
  input  in_1,
  input  [31:0] in_2,
  input  [31:0] in_3,
  input  [31:0] in_4,
  input  [25:0] in_5,
  input  [2:0] in_6,
  input  [31:0] in_7,
  output [31:0] Output
);

  wire [1:0] j;
  wire [31:0] adder_1_out, adder_2_out, multiplier_1_out;

  Adder #(.width(32)) adder_1 (.a(in_4), .b(32'h4), .out(adder_1_out));  // open: cin, cout
  Multiplier #(.width(32)) multiplier_1 (.a(in_7), .b(32'h4), .out(multiplier_1_out));  // open: cin, cout
  Branch_Operation branch_operation_1 (.Rs(in_2), .Rt(in_3), .Code(in_6), .j(j));
  Adder #(.width(32)) adder_2 (.a(adder_1_out), .b(multiplier_1_out), .out(adder_2_out));  // open: cin, cout
  Multiplexer #(.select(2), .width(32)) multiplexer_1 (
    .in0(adder_1_out), .in1(adder_2_out), .in2({in_4[31:28], in_5, 2'b00}), .in3(in_2), .out(Output), .sel(j));  // open: en
  // Probe on j

  // Other names for the same wires on the sheet: Destino_Salto[25:0] = in_5; IA[31:0] = in_4; A[31:0] = in_2;
  //   B[31:0] = in_3; Constant[31:0] = in_7; jmp = in_1; Sb[2:0] = in_6
endmodule

// Br Op
module Branch_Operation (
  input  [31:0] Rs,
  input  [31:0] Rt,
  input  [2:0] Code,
  output [1:0] j
);

  wire beq, bgtz, blez, bltz, bne, branch_selector_1_flag_condition, comparator_2_eq, decoder_1_out0,
       decoder_1_out1, decoder_1_out2, decoder_1_out3, decoder_1_out4, j_t, jr;

  Decoder #(.select(3), .enable("false")) decoder_1 (
    .out0(decoder_1_out0), .out1(decoder_1_out1), .out2(decoder_1_out2), .out3(decoder_1_out3),
    .out4(decoder_1_out4), .out5(j_t), .out6(jr), .sel(Code));  // open: out7
  Comparator #(.width(32)) comparator_1 (.a(Rs), .b(Rt), .eq(beq));  // open: gt, lt
  not not_1 (bne, beq);
  Comparator #(.width(32)) comparator_2 (.a(Rs), .b({32{1'b0}}), .gt(bgtz), .eq(comparator_2_eq), .lt(bltz));
  // Probe on Rs
  or or_1 (blez, comparator_2_eq, bltz);
  Branch_Selector branch_selector_1 (
    .Op_beq(decoder_1_out0), .Cond_beq(beq), .Op_bne(decoder_1_out1), .Cond_bne(bne),
    .Op_blez(decoder_1_out2), .Cond_blez(blez), .Op_bgtz(decoder_1_out3), .Cond_bgtz(bgtz),
    .Op_bltz(decoder_1_out4), .Cond_bltz(bltz), .Flag_Condition(branch_selector_1_flag_condition));
  or or_2 (j[0], branch_selector_1_flag_condition, jr);
  or or_3 (j[1], jr, j_t);
endmodule

module Branch_Selector (
  input  Op_beq,
  input  Cond_beq,
  input  Op_bne,
  input  Cond_bne,
  input  Op_blez,
  input  Cond_blez,
  input  Op_bgtz,
  input  Cond_bgtz,
  input  Op_bltz,
  input  Cond_bltz,
  output Flag_Condition
);

  wire and_1_out, and_2_out, and_3_out, and_4_out, and_5_out;

  and and_1 (and_1_out, Op_beq, Cond_beq);
  and and_2 (and_2_out, Op_bne, Cond_bne);
  and and_3 (and_3_out, Op_blez, Cond_blez);
  and and_4 (and_4_out, Op_bgtz, Cond_bgtz);
  and and_5 (and_5_out, Op_bltz, Cond_bltz);
  or or_1 (Flag_Condition, and_1_out, and_2_out, and_3_out, and_4_out, and_5_out);
endmodule

module Instruction_Register (
  input  [31:0] Instruction,
  input  in_2,
  input  in_3,
  input  in_4,
  output [31:0] Output,
  output Instruction_Charged
);

  wire comparator_1_eq, comparator_2_eq;

  Register #(.width(32)) register_1 (
    .D(Instruction), .en(in_4), .Q({Output[7:0], Output[15:8], Output[23:16], Output[31:24]}), .clk(in_2),
    .clr(in_3));
  Comparator #(.width(32)) comparator_1 (
    .a({Output[7:0], Output[15:8], Output[23:16], Output[31:24]}), .b(Instruction), .eq(comparator_1_eq));  // open: gt, lt
  Comparator #(.width(32)) comparator_2 (.a(Instruction), .b({32{1'b0}}), .eq(comparator_2_eq));  // open: gt, lt
  and and_1 (Instruction_Charged, comparator_1_eq, ~comparator_2_eq);  // AND_Gate

  // Other names for the same wires on the sheet: Clock = in_2; enable = in_4; reset = in_3
endmodule

module Memory_Address (
  input  [31:0] PC,
  input  [31:0] ALU,
  input  [31:0] SP,
  input  lw,
  input  sw,
  input  pop,
  input  push,
  input  pc_2,
  output [31:0] Output
);

  wire [1:0] or_2_out;
  wire [31:0] multiplexer_1_out, subtractor_1_out;

  Multiplexer #(.width(32), .enable("false")) multiplexer_1 (
    .in0(SP), .in1(subtractor_1_out), .out(multiplexer_1_out), .sel(push));
  Subtractor #(.width(32)) subtractor_1 (.a(SP), .b(32'h4), .out(subtractor_1_out));  // open: bin, bout
  or or_1 (or_2_out[1], pop, pc_2, push);
  Multiplexer #(.select(2), .width(32), .enable("false")) multiplexer_2 (
    .in0(PC), .in1(ALU), .in2(multiplexer_1_out), .in3(PC), .out(Output), .sel(or_2_out));
  or or_2 (or_2_out[0], lw, pc_2, sw);

  // Other names for the same wires on the sheet: isPC = pc_2
endmodule

module Memorie (
  input  [31:0] Address,
  input  [31:0] RAM_Out_0,
  input  [31:0] RAM_Out_1,
  input  [31:0] RAM_Out_2,
  input  [31:0] RAM_Out_3,
  input  [3:0] in_6,
  input  [3:0] in_7,
  input  Clock,
  input  Reset,
  input  Write,
  input  Obtain_Inst,
  input  Obtain_Data,
  input  Is_Instruction,
  input  Halt,
  output [31:0] RAM_In_0,
  output [31:0] RAM_In_1,
  output [31:0] RAM_In_2,
  output [31:0] RAM_In_3,
  output [15:0] Output,
  output [3:0] Output_2,
  output Output_3,
  output Output_4,
  output Output_5,
  output Output_6,
  output Output_7
);

  wire CSI, or_1_out, stop, WCS;
  wire [31:0] output_data_block_0, output_data_block_1, output_data_block_2, output_data_block_3,
       output_instruction_block_0, output_instruction_block_1, output_instruction_block_2,
       output_instruction_block_3;

  Multiplexer #(.width(32), .enable("false")) multiplexer_1 (
    .in0({output_data_block_0[7:0], output_data_block_0[15:8], output_data_block_0[23:16], output_data_block_0[31:24]}),
    .in1(output_instruction_block_0), .out(RAM_In_0), .sel(Is_Instruction));
  Multiplexer #(.width(32), .enable("false")) multiplexer_2 (
    .in0({output_data_block_3[7:0], output_data_block_3[15:8], output_data_block_3[23:16], output_data_block_3[31:24]}),
    .in1(output_instruction_block_3), .out(RAM_In_3), .sel(Is_Instruction));
  or or_1 (or_1_out, Write, stop);
  D_Flip_Flop #(.trigger("falling")) d_ff_1 (
    .clk(Clock), .D(Write), .Q(Output_4), .en(or_1_out));  // open: Qn, preset, reset
  Instruction_Memory instruction_memory_1 (
    .instruction_block_0(RAM_Out_0), .instruction_block_1(RAM_Out_1), .instruction_block_2(RAM_Out_2),
    .instruction_block_3(RAM_Out_3), .in_6(in_6), .Reset(Reset), .Obtain_Instruction(Obtain_Inst),
    .Halt(Halt), .Clock(Clock), .Chip_Select(CSI), .output_block_0(output_instruction_block_0),
    .output_block_1(output_instruction_block_1), .output_block_2(output_instruction_block_2),
    .output_block_3(output_instruction_block_3), .Ready(Output_5), .Address(Address));
  Data_Memory data_memory_1 (
    .Address(Address), .output_block_0(output_data_block_0), .data_block_0(RAM_Out_0),
    .output_block_1(output_data_block_1), .data_block_1(RAM_Out_1), .output_block_2(output_data_block_2),
    .data_block_2(RAM_Out_2), .output_block_3(output_data_block_3), .data_block_3(RAM_Out_3), .in_6(in_6),
    .Clock(Clock), .Reset(Reset), .Obtain_Data(Obtain_Data), .WCS(WCS), .Ready(Output_6));
  Timer timer_1 (.Time(in_7), .Ready(stop), .Clock(Clock), .Reset(Output_7), .Start(Output_4));
  Multiplexer #(.width(32), .enable("false")) multiplexer_3 (
    .in0({output_data_block_2[7:0], output_data_block_2[15:8], output_data_block_2[23:16], output_data_block_2[31:24]}),
    .in1(output_instruction_block_2), .out(RAM_In_2), .sel(Is_Instruction));
  D_Flip_Flop #(.trigger("falling")) d_ff_2 (.clk(Clock), .D(stop), .Q(Output_7));  // open: Qn, preset, en, reset
  Multiplexer #(.width(32), .enable("false")) multiplexer_4 (
    .in0({output_data_block_1[7:0], output_data_block_1[15:8], output_data_block_1[23:16], output_data_block_1[31:24]}),
    .in1(output_instruction_block_1), .out(RAM_In_1), .sel(Is_Instruction));
  or or_2 (Output_3, CSI, WCS, Output_4);
  Address_Separator address_separator_1 (.Address(Address), .Mask(Output_2), .RAM_Address(Output));

  // Other names for the same wires on the sheet: address_t[15:0] = Output; Clck = Clock; CS = Output_3;
  //   is_inst = Is_Instruction; mask[3:0] = Output_2; RAM_INPUT_0[31:0] = RAM_In_0; RAM_INPUT_1[31:0] = RAM_In_1;
  //   RAM_INPUT_2[31:0] = RAM_In_2; RAM_INPUT_3[31:0] = RAM_In_3; RAM_OUTPUT_0[31:0] = RAM_Out_0;
  //   RAM_OUTPUT_1[31:0] = RAM_Out_1; RAM_OUTPUT_2[31:0] = RAM_Out_2; RAM_OUTPUT_3[31:0] = RAM_Out_3;
  //   read_time[3:0] = in_6; ready_data = Output_6; ready_inst = Output_5; ready_write = Output_7; RW = Output_4;
  //   write_time[3:0] = in_7

  // Notes on the sheet:
  //   DATA FROM RAM
  //   DATA TO RAM
endmodule

module Timer (
  input  [3:0] Time,
  input  Start,
  input  Clock,
  input  Reset,
  output Ready
);

  wire [3:0] counter_1_q;

  Counter #(.width(4), .max('hf)) counter_1 (
    .count(Start), .Q(counter_1_q), .clk(Clock), .clr(Reset));  // open: load, D, carry
  Comparator #(.width(4)) comparator_1 (.a(Time), .b(counter_1_q), .eq(Ready));  // open: gt, lt
endmodule

// AS
module Address_Separator (
  input  [31:0] Address,
  output [3:0] Mask,
  output [15:0] RAM_Address
);

  Demultiplexer #(.select(2), .enable("false")) demultiplexer_1 (
    .out0(Mask[0]), .out1(Mask[1]), .out2(Mask[2]), .out3(Mask[3]), .in(1'b1), .sel(Address[3:2]));

  assign RAM_Address = Address[19:4];
endmodule
